# Fritzing sketch connections (saved by Fritzing 0.9.5d)

parts:
  WeMos_D1_Mini1 = WeMos D1 Mini
  U1 = 2-Channel 5v Relay Shield [package=relay-2ch5v10a]
  Part1 = OLED Monochrome 128x32 I2C [part_number=931]
  S1 = Round Pushbutton
  Part2 = Adafruit Thermocouple Amplifier MAX31855 [part_number="Adafruit #269"]
  R3 = Temperature Sensor (Thermistor) [thermistor_type=NTC package=THT]
  R4 = Temperature Sensor (Thermistor) [thermistor_type=NTC package=THT]
  R5 = Resistor [tolerance=±5% resistance=220 package="2512 [SMD]"]

nets:
  3V3: WeMos_D1_Mini1.3V3, Part1.3.3V, Part2.+3V3, R5.Pin_1
  5V: WeMos_D1_Mini1.5V, U1.VCC
  N1: WeMos_D1_Mini1.A0, R4.pin_1, R5.Pin_0
  N2: WeMos_D1_Mini1.D0, U1.IN2
  N3: WeMos_D1_Mini1.D1, Part1.SCL
  N4: WeMos_D1_Mini1.D2, Part1.SDA
  N5: WeMos_D1_Mini1.D3, S1.leg0
  N6: WeMos_D1_Mini1.D4, U1.IN1
  N7: WeMos_D1_Mini1.D5, Part2.CLK
  N8: WeMos_D1_Mini1.D6, Part2.DO
  N9: WeMos_D1_Mini1.D8, Part2.CS
  GND: WeMos_D1_Mini1.G, U1.GND, Part1.GND, S1.leg1, Part2.GND, R4.pin_0
  N10: Part2.THERMO-, R3.pin_0
  N11: Part2.THERMO+, R3.pin_1

custom parts:
  2-Channel 5v Relay Shield: 2 Channel 5v Relay Shield w. 2x SPD-06VDC-SD-C
  OLED Monochrome 128x32 I2C: These displays are small, only about 1" diagonal, but very readable due to the high contrast of an OLED display. This display is made of 128x32 individual white OLED pixels, each one is turned on or off by the controller chip. Because the display makes its own light, no backlight is required. This reduces the power required to run the OLED and is why the display has such high contrast; we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
  Adafruit Thermocouple Amplifier MAX31855: Thermocouples are very sensitive, requiring a good amplifier with a cold-compensation reference. The MAX31855K does everything for you, and can be easily interfaced with any microcontroller, even one without an analog input. This breakout board has the chip itself, a 3.3V regulator with 10uF bypass capacitors and level shifting circuitry, all assembled and tested. Comes with a 2 pin terminal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
